# Fritzing sketch stocks (saved by Fritzing 1.0.6)
stripboards: 1
breadboards: 1

parts:
  Arduino = Arduino Uno (Rev3)
  NHD-0420DZ-FSW-FBW = LCD screen
  R2 = Resistor [tolerance=±5% power=0.25 resistance=20k package=THT]
  R3 = Resistor [tolerance=±5% power=0.25 resistance=1k package=THT]

nets:
  N1: Arduino.A0, Arduino.A1, Arduino.A2, Arduino.A3, Arduino.A4/SDA, Arduino.A5/SCL, Arduino.GND, NHD-0420DZ-FSW-FBW.R/W, NHD-0420DZ-FSW-FBW.LED-
  N2: Arduino.D2, NHD-0420DZ-FSW-FBW.DB7
  N3: Arduino.D3_PWM, NHD-0420DZ-FSW-FBW.DB6
  N4: Arduino.D4, NHD-0420DZ-FSW-FBW.DB5
  N5: Arduino.D5_PWM, NHD-0420DZ-FSW-FBW.DB4
  N6: Arduino.D6_PWM, NHD-0420DZ-FSW-FBW.E
  N7: Arduino.D7, NHD-0420DZ-FSW-FBW.RS
  5V: Arduino.5V, NHD-0420DZ-FSW-FBW.VDD, NHD-0420DZ-FSW-FBW.LED+, R2.Pin_0
  N8: NHD-0420DZ-FSW-FBW.VSS, R3.Pin_1
  N9: NHD-0420DZ-FSW-FBW.V0, R2.Pin_1, R3.Pin_0

notes:
  wires to cut
